# Fritzing sketch ACMS_1 (saved by Fritzing 0.9.2b)
breadboards: 1

parts:
  Part1 = Arduino Uno (Rev3)
  U1 = NodeMCU V1.0  # not connected
  Load_Cell1 = Load Cell - Red/white/black/green
  Part3 = HX711 Weighing Sensor Module
  Display1 = LCD screen 16x2 IIC [part_number=101290]
  Mod1 = MQ-7 breakout
  F1 = Fan - Ventilador [package=THT]
  M1 = L293D Motor Driver
  VCC1 = Battery block 9V  # not connected
  J1 = Piezo Speaker
  Part4 = DC-DC Power Module (5v)  # not connected
  Part5 = Lilypad Battery Connect
  Part6 = DC-DC Power Module (5v)

nets:
  N1: Part1.A0, Mod1.AO
  N2: Part1.A4/SDA, Display1.SDA
  N3: Part1.A5/SCL, Display1.SCL
  N4: Part1.D9_PWM, J1.pin2
  N5: Part1.D2, Part3.CK/TX
  N6: Part1.D3_PWM, Part3.DO/RX
  N7: Part1.D4, M1.pin_5
  3V3: Part1.3V3, Part3.VCC
  VCC: Part1.5V, Display1.VCC, Mod1.VCC
  GND: Part1.GND, Part3.GND, Display1.GND, Mod1.GND, M1.pin_6, J1.pin1, Part6.GND*
  N8: Part1.VIN, Part6.Vout
  N9: Load_Cell1.wire1, Part3.E+
  N10: Load_Cell1.wire2, Part3.A-
  N11: Load_Cell1.wire3, Part3.E-
  N12: Load_Cell1.wire4, Part3.A+
  N13: F1.5V, M1.pin_9
  N14: F1.GND, M1.pin_10
  N15: Part5.-, Part6.GND
  N16: Part5.+, Part6.Vin

notes:
  Fan
  L293D
  9V Battery
  20kg Loadcell
  HX711
  MQ6 Gas sensor
  LCD Display// IIC
  NodeMCU ESP8266
  Buzzer
  UNO
  AC 230V
  Adapter

custom parts:
  NodeMCU V1.0: ESP8266 based NodeMCU
  Load Cell - Red/white/black/green: A rectangle load cell/weighting pressure Sensor with four wires - Red, white, black, green. Normally corresponding with E+, E-, A+, A- respectively.
  HX711 Weighing Sensor Module: HX711 is a precision 24-bit analog-to-digital converter (ADC) designed for weigh scales and industrial control applications to interface directly with a bridge sensor.
  LCD screen 16x2 IIC: LCD screen with HD44780 controller enables showing text, symbols, value or anything else that comes from Croduino/Arduino. It is capable of showing 16 symbols in two lines and therefore can be used in many projects that need to send clearly visible and legible output information.. • Color of symbols: White • Backlight: Blue • Dimensions: 80 x 36 x 12 mm • Screen dimensions: 64.5 x 16 mm •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
  MQ-7 breakout: MQ-5 gas sensor
  Fan - Ventilador: Ventilador de 2 pines, se encuentra comunmente en computadoras de escritorio
  DC-DC Power Module (5v): DC-DC Power Module based con AMS1117-5.0 Input: DC 6~12V (input power must higher 1V than output power); Output: 5V (+/-0.05V error), 800mA
