# Fritzing sketch ACMS_2 (saved by Fritzing 0.9.2b)
breadboards: 1

parts:
  Part1 = Arduino Uno (Rev3)
  Load_Cell1 = Load Cell - Red/white/black/green
  Part3 = HX711 Weighing Sensor Module
  Display1 = LCD screen 16x2 IIC [part_number=101290]
  Mod1 = MQ-7 breakout
  F1 = Fan - Ventilador [package=THT]
  M1 = L293D Motor Driver
  VCC1 = Battery block 9V  # not connected
  J1 = Piezo Speaker
  SIM800L_BO1 = SIM800L BO
  U1 = LM2596 step down module
  Part4 = DC-DC Power Module (5v)
  Part6 = Lilypad Battery Connect
  Part7 = DC-DC Power Module (5v)

nets:
  N1: Part1.A0, Mod1.AO
  N2: Part1.A4/SDA, Display1.SDA
  N3: Part1.A5/SCL, Display1.SCL
  N4: Part1.D9_PWM, J1.pin2
  N5: Part1.D0/RX, SIM800L_BO1.pin_5
  N6: Part1.D1/TX, SIM800L_BO1.pin_4
  N7: Part1.D2, Part3.CK/TX
  N8: Part1.D3_PWM, Part3.DO/RX
  N9: Part1.D4, M1.pin_5
  3V3: Part1.3V3, Part3.VCC
  VCC: Part1.5V, Display1.VCC, Mod1.VCC
  GND: Part1.GND, Part3.GND, Display1.GND, Mod1.GND, M1.pin_6, J1.pin1
  N10: Part1.VIN, Part7.Vout
  N11: Load_Cell1.wire1, Part3.E+
  N12: Load_Cell1.wire2, Part3.A-
  N13: Load_Cell1.wire3, Part3.E-
  N14: Load_Cell1.wire4, Part3.A+
  N15: F1.5V, M1.pin_9
  N16: F1.GND, M1.pin_10
  N17: SIM800L_BO1.PIN2, U1.OUT+
  N18: SIM800L_BO1.pin_6, U1.IN-, U1.OUT-, Part4.GND*
  N19: U1.IN+, Part4.Vout
  N20: Part6.-, Part7.GND
  N21: Part6.+, Part7.Vin

notes:
  Fan
  L293D
  9V Battery
  20kg Loadcell
  HX711
  MQ6 Gas sensor
  LCD Display// IIC
  Buzzer
  UNO
  LM2596
  SIM800l
  Adapter 7V
  AC 230V

custom parts:
  Load Cell - Red/white/black/green: A rectangle load cell/weighting pressure Sensor with four wires - Red, white, black, green. Normally corresponding with E+, E-, A+, A- respectively.
  HX711 Weighing Sensor Module: HX711 is a precision 24-bit analog-to-digital converter (ADC) designed for weigh scales and industrial control applications to interface directly with a bridge sensor.
  LCD screen 16x2 IIC: LCD screen with HD44780 controller enables showing text, symbols, value or anything else that comes from Croduino/Arduino. It is capable of showing 16 symbols in two lines and therefore can be used in many projects that need to send clearly visible and legible output information.. • Color of symbols: White • Backlight: Blue • Dimensions: 80 x 36 x 12 mm • Screen dimensions: 64.5 x 16 mm •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
  MQ-7 breakout: MQ-5 gas sensor
  Fan - Ventilador: Ventilador de 2 pines, se encuentra comunmente en computadoras de escritorio
  LM2596 step down module: LM2596 DC-DC step down power supply module 3 A.
  DC-DC Power Module (5v): DC-DC Power Module based con AMS1117-5.0 Input: DC 6~12V (input power must higher 1V than output power); Output: 5V (+/-0.05V error), 800mA
